// Logisim project Lab2.circ as structural Verilog
module Lab2 (
  input  A1,
  input  A0,
  input  B1,
  input  B0,
  input  [3:0] In,
  input  B1_2,
  input  B0_2,
  input  A1_2,
  input  A0_2,
  output ALessThanOrEqualToB,
  output A__B,
  output A__B_2
);

  wire and_1_out, and_2_out, and_3_out, and_4_out, and_5_out, not_1_out, not_2_out, not_3_out, not_4_out,
       not_5_out, not_6_out;

  not not_1 (not_1_out, A1);
  and and_1 (and_1_out, not_1_out, not_2_out);
  not not_2 (not_2_out, A0);
  not not_3 (not_3_out, A1);
  and and_2 (and_2_out, not_3_out, B0);
  not not_4 (not_4_out, A1);
  and and_3 (and_3_out, not_4_out, B1);
  not not_5 (not_5_out, A0);
  and and_4 (and_4_out, not_5_out, B1);
  and and_5 (and_5_out, B1, B0);
  not not_6 (not_6_out, B1_2);
  or or_1 (ALessThanOrEqualToB, and_1_out, and_2_out, and_3_out, and_4_out, and_5_out);
  Multiplexer #(.select(3), .enable("false")) multiplexer_1 (
    .in0(1'b1), .in1(1'b1), .in2(not_6_out), .in3(1'b1), .in4(1'b0), .in5(1'b1), .in6(1'b0), .in7(B1_2),
    .out(A__B_2), .sel({A1_2, B0_2, B1_2}));
  ROM #(.addrWidth(4), .dataWidth(1)) rom_1 (.addr(In), .data(A__B));  // open: sel
  // Pins of 3 and 4 bits meet at {A0_2, A1_2, B0_2, B1_2}

  // Notes on the sheet:
  //   contents of rom_1 (hex, n*v repeats v):
  //   4*1 0 1 1 1 0 0 1 1 0 0 0 1
endmodule

module Lab2_2 (
  input  X,
  input  Y,
  input  [2:0] in_3,
  input  Z,
  input  X_2,
  input  Y_2,
  input  Z_2,
  output Minority,
  output Minority_2,
  output Minority_3
);

  wire and_1_out, and_2_out, and_3_out, not_1_out, not_2_out, not_3_out, not_4_out, not_5_out, not_6_out;

  not not_1 (not_1_out, X);
  not not_2 (not_2_out, Y);
  not not_3 (not_3_out, X);
  not not_4 (not_4_out, Z);
  not not_5 (not_5_out, Y);
  not not_6 (not_6_out, Z);
  and and_1 (and_1_out, not_1_out, not_2_out);
  and and_2 (and_2_out, not_3_out, not_4_out);
  and and_3 (and_3_out, not_5_out, not_6_out);
  or or_1 (Minority, and_1_out, and_2_out, and_3_out);
  Multiplexer #(.select(3), .enable("false")) multiplexer_1 (
    .in0(1'b1), .in1(1'b1), .in2(1'b1), .in3(1'b0), .in4(1'b1), .in5(1'b0), .in6(1'b0), .in7(1'b0),
    .out(Minority_3), .sel({Z_2, Y_2, X_2}));
  ROM #(.addrWidth(3), .dataWidth(1)) rom_1 (.addr(in_3), .data(Minority_2));  // open: sel

  // Notes on the sheet:
  //   contents of rom_1 (hex, n*v repeats v):
  //   1 1 1 0 1
endmodule
